# Fritzing sketch usb-cable-load (saved by Fritzing 0.9.2b)
circuit board: 5.13cm x 6.33cm
breadboards: 1

parts:
  USB_B = USB+SHIELD [package=usb-b-pth]
  D4 = Schottky Diode [part_number=1N5817 package="300 mil [THT]"]
  D3 = Schottky Diode [part_number=1N5817 package="300 mil [THT]"]
  D1 = Schottky Diode [part_number=1N5817 package="300 mil [THT]"]
  D2 = Schottky Diode [part_number=1N5817 package="300 mil [THT]"]
  USB_A = USB Connectors [package=usb-a-h]
  R1 = 10W Resistor [package=THT]
  miniUSB = Mini-USB _B_ connector with 5th pin broken out. [package=usb-minib]
  microUSB = USB_AB [package=usb-ab-micro-smd]

nets:
  GND: USB_B.GND, USB_A.GND, R1.Pin_1, miniUSB.GND, microUSB.GND
  N1: USB_B.VBUS, D4.anode
  N2: D4.cathode, D3.cathode, D1.cathode, D2.cathode, R1.Pin_0
  N3: D3.anode, USB_A.VBUS
  N4: D1.anode, miniUSB.VBUS
  N5: D2.anode, microUSB.VBUS

custom parts:
  10W Resistor: Cement resistor (10W)
